// Logisim project Controleur.circ as structural Verilog
module main (
  input  FLAG,
  input  [31:0] SortirFromCheminDeDonnes,
  output [3:0] Ra,
  output [3:0] Rb,
  output [3:0] Rd,
  output [3:0] CodeOp
);

  wire Clock_out;
  wire [7:0] adder_1_out, bitselector_1_out, multiplexer_1_out, undriven;
  wire [15:0] rom_1_data;

  ROM #(.dataWidth(16)) rom_1 (.addr(adder_1_out), .data(rom_1_data));
  Register #(.width(16)) RI (.D(rom_1_data));  // open: en, clk, Q, clr
  Clock Clock (.out(Clock_out));
  Multiplexer #(.width(8), .enable("false")) multiplexer_1 (
    .in0(bitselector_1_out), .in1(undriven), .out(multiplexer_1_out));  // open: sel
  Adder adder_1 (.a(multiplexer_1_out), .b(8'h4), .out(adder_1_out));  // open: cin, cout
  Register PC (.D(adder_1_out), .clk(Clock_out), .Q(adder_1_out));  // open: en, clr
  Controleur controleur_1 ();
  BitSelector #(.width(32), .group(8)) bitselector_1 (
    .in(SortirFromCheminDeDonnes), .out(bitselector_1_out), .sel(2'b11));

  // Notes on the sheet:
  //   contents of rom_1 (hex, n*v repeats v):
  //   1 10 11 100 101 110 111 1000 1001 1011 1100 1101 1100 1101 1110 1111
endmodule

module DataProcessing (
  input  b0,
  input  b1,
  input  b2,
  input  b3,
  input  b4,
  input  b5,
  input  b6,
  input  b7,
  input  b8,
  input  b9,
  input  b10,
  input  b11,
  input  b12,
  input  b13,
  input  b14,
  input  b15,
  input  [15:0] PC,
  output [2:0] R,
  output [2:0] R_2,
  output [2:0] R_3,
  output [3:0] ULACode,
  output [5:0] OpcodeData
);

  Comparator comparator_1 ();  // open: a, b, gt, eq, lt
  // Pins of 1 and 2 bits meet at {PC[15], b14}

  assign OpcodeData = {b15, b14, b13, b12, b11, b10};
  assign PC[14:0] = {b14, b13, b12, b11, b10, b9, b8, b7, b6, b5, b4, b3, b2, b1, b0};
  assign R_2 = {b2, b1, b0};
  assign R_3 = {b5, b4, b3};
  assign ULACode = {b9, b8, b7, b6};
endmodule
